// Logisim project william, equality.1814905.circ as structural Verilog: 2 circuits, main circuit equality
module main (
  input  x,
  input  y,
  output out_3
);

  wire and_1_out, and_2_out, not_1_out, not_2_out, or_1_out;

  not not_1 (not_1_out, x);
  not not_2 (not_2_out, y);
  and and_1 (and_1_out, not_1_out, y);
  and and_2 (and_2_out, x, not_2_out);
  or or_1 (or_1_out, and_1_out, and_2_out);
  not not_3 (out_3, or_1_out);
endmodule

module equality (
  input  [2:0] in_1,
  input  [2:0] in_2,
  output out_3
);

  wire main_1_out_3, main_2_out_3, main_3_out_3;

  main main_1 (.x(in_1[0]), .y(in_2[0]), .out_3(main_1_out_3));
  main main_2 (.x(in_1[1]), .y(in_2[1]), .out_3(main_2_out_3));
  main main_3 (.x(in_1[2]), .y(in_2[2]), .out_3(main_3_out_3));
  and and_1 (out_3, main_1_out_3, main_2_out_3, main_3_out_3);
endmodule
